// Logisim project ROM ZSelect.circ as structural Verilog: 1 circuit, main circuit main
module main (
  input  minus_reset,
  input  A15,
  output out_3,
  output out_4,
  output out_5,
  output out_6,
  output out_7
);

  // IC_7474 ic_7474_1: pin names not known; wires that end beside it: 1'b0, A15, minus_reset, 1'b1, out_3
  // IC_74157 ic_74157_1: pin names not known; wires that end beside it: 1'b0, 1'b1, 1'b0, 1'b1, 1'b0, 1'b1, 1'b0, 1'b1, out_3, 1'b0, out_4, out_5, out_6, out_7
endmodule
