// Logisim project testcircuit.circ as structural Verilog: 1 circuit, main circuit main
module main (
  input  A0,
  input  minus_BRD_SEL,
  input  A1,
  input  minus_BUS_EN,
  input  RD
);

  wire BRD_SEL, n74138_1_p7, n74138_1_p8, n74138_1_p9, n74138_1_p10, n74138_1_p11, n74138_1_p12,
       n74138_1_p13, n74138_1_p14, n74138_2_p7, n74138_2_p8, n74138_2_p9, n74138_2_p10, n74138_2_p11,
       n74138_2_p12, n74138_2_p13, n74138_2_p14, n74374_1_p11, n74374_1_p12, n74374_1_p13, n74374_1_p14,
       n74374_1_p15, n74374_1_p16, n74374_1_p17, n74374_1_p18, n74374_2_p11, n74374_2_p12, n74374_2_p13,
       n74374_2_p14, n74374_2_p15, n74374_2_p16, n74374_2_p17, n74374_2_p18, nand_1_out, nand_2_out,
       or_1_out, or_2_out;

  or or_1 (or_1_out, minus_BUS_EN, nand_1_out);
  nand nand_1 (nand_1_out, RD, RD);
  nand nand_2 (nand_2_out, RD, RD);
  not not_1 (BRD_SEL, minus_BRD_SEL);
  or or_2 (or_2_out, minus_BUS_EN, nand_2_out);
  // _74138 74138_1: pin names not known; wires that end beside it: 1'b1, 1'b0, minus_BRD_SEL, A0, A1, 1'b0, n74138_1_p7, n74138_1_p8, n74138_1_p9, n74138_1_p10, n74138_1_p11, n74138_1_p12, n74138_1_p13, n74138_1_p14
  // _74138 74138_2: pin names not known; wires that end beside it: 1'b1, 1'b0, BRD_SEL, A0, A1, 1'b0, n74138_2_p7, n74138_2_p8, n74138_2_p9, n74138_2_p10, n74138_2_p11, n74138_2_p12, n74138_2_p13, n74138_2_p14
  // _74374 74374_1: pin names not known; wires that end beside it: n74138_1_p7, n74138_1_p8, n74138_1_p9, n74138_1_p10, n74138_1_p11, n74138_1_p12, n74138_1_p13, n74138_1_p14, or_1_out, RD, n74374_1_p11, n74374_1_p12, n74374_1_p13, n74374_1_p14, n74374_1_p15, n74374_1_p16, n74374_1_p17, n74374_1_p18, n74374_1_p13, n74374_1_p14, n74374_1_p15, n74374_1_p16, n74374_1_p17, n74374_1_p18
  // _74374 74374_2: pin names not known; wires that end beside it: n74138_2_p7, n74138_2_p8, n74138_2_p9, n74138_2_p10, n74138_2_p11, n74138_2_p12, n74138_2_p13, n74138_2_p14, or_2_out, RD, n74374_2_p11, n74374_2_p12, n74374_2_p13, n74374_2_p14, n74374_2_p15, n74374_2_p16, n74374_2_p17, n74374_2_p18, n74374_2_p12, n74374_2_p13, n74374_2_p14, n74374_2_p15, n74374_2_p16, n74374_2_p17, n74374_2_p18
  Pull_Resistor #(.pull(1)) pull_resistor_1 (.node(n74374_1_p12));
  // Probe on n74374_1_p11
  // Probe on n74374_1_p12
  // Probe on n74374_2_p11
endmodule
